# Fritzing sketch stereotaxic wiring v1 (saved by Fritzing 1.0.4)
breadboards: 3

parts:
  IC3 = Hex Inverter Schmitt Trigger SN74HC14 [package="DIP (Dual Inline)"]
  IC4 = SHIFT REGISTER [package=dil16]
  IC5 = SHIFT REGISTER [package=dil16]
  IC6 = Hex Inverter Schmitt Trigger SN74HC14 [package="DIP (Dual Inline)"]
  Raspberry_Pi_1 = Raspberry Pi 3 [part_number=RPI-3-V1.2]
  U1 = ENCODER-QUADRATURE [package=encoder-16mm-quad]
  U2 = ENCODER-QUADRATURE [package=encoder-16mm-quad]
  U3 = ENCODER-QUADRATURE [package=encoder-16mm-quad]
  S3 = Pushbutton [package="[THT]"]
  S4 = Pushbutton [package="[THT]"]
  S5 = Pushbutton [package="[THT]"]
  Part1 = EasyDriver_v44
  Part2 = EasyDriver_v44
  Part3 = EasyDriver_v44
  S6 = Momentary Switch [package=ksa_sealed_tac_switch]
  S7 = Momentary Switch [package=ksa_sealed_tac_switch]
  S8 = Momentary Switch [package=ksa_sealed_tac_switch]
  S9 = Momentary Switch [package=ksa_sealed_tac_switch]
  S10 = Momentary Switch [package=ksa_sealed_tac_switch]
  S11 = Momentary Switch [package=ksa_sealed_tac_switch]
  S12 = Momentary Switch [package=ksa_sealed_tac_switch]
  S13 = Momentary Switch [package=ksa_sealed_tac_switch]
  S14 = Momentary Switch [package=ksa_sealed_tac_switch]
  S15 = Momentary Switch [package=ksa_sealed_tac_switch]
  S16 = Momentary Switch [package=ksa_sealed_tac_switch]
  S17 = Momentary Switch [package=ksa_sealed_tac_switch]
  S18 = Momentary Switch [package=ksa_sealed_tac_switch]
  S19 = Momentary Switch [package=ksa_sealed_tac_switch]
  S20 = Momentary Switch [package=ksa_sealed_tac_switch]
  IC7 = Hex Inverter Schmitt Trigger SN74HC14 [package="DIP (Dual Inline)"]
  R1 = Resistor [tolerance=±5% resistance=10k package="1206 [SMD]"]
  R2 = Resistor [tolerance=±5% resistance=10k package="1206 [SMD]"]
  R3 = Resistor [tolerance=±5% resistance=10k package="1206 [SMD]"]
  R4 = Resistor [tolerance=±5% resistance=10k package="1206 [SMD]"]
  R5 = Resistor [tolerance=±5% resistance=10k package="1206 [SMD]"]
  R6 = Resistor [tolerance=±5% resistance=10k package="1206 [SMD]"]

nets:
  N1: IC3.1A, S12.1
  N2: IC3.1Y, IC5.QD
  N3: IC3.2A, S13.1
  N4: IC3.2Y, IC5.QE
  N5: IC3.3A, S14.1
  N6: IC3.3Y, IC5.QF
  GND: IC3.GND, IC4.GND, IC4.QA, IC5.GND, IC5.QA, IC6.GND, Raspberry_Pi_1.GIPO10, Raspberry_Pi_1.GIPO11, Raspberry_Pi_1.GND, Raspberry_Pi_1.GIPO26, U1.B, U3.B, S3.Pin_1, S3.Pin_2, S4.Pin_1, S4.Pin_2, S5.Pin_1, S5.Pin_2, Part1.GND, IC7.GND
  N7: IC3.4Y, IC5.G
  N8: IC3.4A, S9.1
  N9: IC3.5Y, IC5.SER
  N10: IC3.5A, S10.1
  N11: IC3.6Y, IC5.QG
  N12: IC3.6A, S11.1
  VCC: IC3.VCC, IC4.VCC, IC5.VCC, IC6.VCC, Raspberry_Pi_1.3v3, Raspberry_Pi_1.3V3, IC7.VCC, R1.Pin_0, R2.Pin_1, R3.Pin_0, R4.Pin_1, R5.Pin_0, R6.Pin_1
  N13: IC4.QD, IC6.1Y
  N14: IC4.QE, IC6.2Y
  N15: IC4.QF, IC6.3Y
  N16: IC4.QG, IC6.4Y
  N17: IC4.QH*, IC5.SCL
  N18: IC4.RCK, IC7.3Y
  N19: IC4.G, IC7.2Y
  N20: IC4.SER, IC7.1Y
  N21: IC5.QB, Raspberry_Pi_1.GIPO18
  N22: IC5.QC, Raspberry_Pi_1.GIPO23
  N23: IC5.QH*, Raspberry_Pi_1.GIPO24
  N24: IC5.SCK, IC6.5Y
  N25: IC5.RCK, IC6.6Y
  N26: IC6.1A, S15.1
  N27: IC6.2A, S16.1
  N28: IC6.3A, S17.1
  N29: IC6.4A, S6.1
  N30: IC6.5A, S7.1
  N31: IC6.6A, S8.1
  N32: Raspberry_Pi_1.GPIO2, Part3.ENABLE
  N33: Raspberry_Pi_1.GPIO3, Part1.DIR
  N34: Raspberry_Pi_1.GIPO4, Part1.STEP
  N35: Raspberry_Pi_1.GIPO17, Part2.DIR
  N36: Raspberry_Pi_1.GIPO27, Part2.STEP
  N37: Raspberry_Pi_1.ID_SD, Part3.DIR
  N38: Raspberry_Pi_1.GIPO5, Part3.STEP
  N39: Raspberry_Pi_1.GIPO21, U1.A, R6.Pin_0
  N40: Raspberry_Pi_1.GIPO20, U1.C, R5.Pin_1
  N41: Raspberry_Pi_1.GIPO16, U3.A, R4.Pin_0
  N42: Raspberry_Pi_1.GIPO12, U3.C, R3.Pin_1
  N43: Raspberry_Pi_1.GIPO8, U2.A, R2.Pin_0
  N44: Raspberry_Pi_1.GIPO25, U2.C, R1.Pin_1
  5V: Raspberry_Pi_1.5V, Part3.VCC
  N45: S3.Pin_3, S3.Pin_4
  N46: S4.Pin_3, S4.Pin_4
  N47: S5.Pin_3, S5.Pin_4
  N48: S18.1, IC7.1A
  N49: S19.1, IC7.2A
  N50: S20.1, IC7.3A
